# Fritzing sketch web_radio_wroom (saved by Fritzing 0.9.4)
breadboards: 1

parts:
  MCU1 = Wemos Lolin32lite
  U2 = WS2812 RGB LED strip
  U3 = lolin
  U4 = 2.4" TFT LCD screen, SPI, Touch-enabled
  U5 = ESP32-38PinWide [part_number=ESP32-38PinWide]  # not connected

nets:
  N1: MCU1.pin_8, U2.DIN
  GND: U2.GND, U3.connector37, U4.GND
  VCC: U2.VCC, U3.connector34, U4.VCC
  N2: U3.connector1, U4.RESET
  N3: U3.connector9, U4.LED
  N4: U3.connector18, U4.CS
  N5: U3.connector19, U4.DC
  N6: U3.connector27, U4.SCL
  N7: U3.connector28, U4.SDA
  N8: U3.connector29, U4.SDO

notes:
  INMP441

custom parts:
  Wemos Lolin32lite: Wemos Lolinlite32 wifi and blue tooth board based on the ESP-32 cpu, digital I/Os 19, analog inputs 6, clock 240mhz, Flash 4Mbytes, lipo battery charger (500ma connection broken out on breadboard but not pcb), usb.
  WS2812 RGB LED strip: WS2812 strip
  2.4" TFT LCD screen, SPI, Touch-enabled: 2.4", ILI9341-based TFT LCD screen with touch-sensing using the XPT2046 controller, SPI-compatible. There is also an SD-card version that is non-touch enabled but uses exactly the same board and pinout. This part is for both, though it should be noted that the SD reader and the touch screen are mutually incompatible
  ESP32-38PinWide: Generic 38-Pin ESP32 with wide format (only access to one side of pins on a breadboard) based on Stephen Lilley's HiLetgo ESP-WROOM-32 ESP32 ESP-32S Development Board.
